// Logisim project mux4v3bCOMP.circ as structural Verilog: 1 circuit, main circuit main
module main (
  input  [2:0] CANAL_0,
  input  [2:0] CANAL_1,
  input  [2:0] CANAL_2,
  input  [2:0] CANAL_3,
  input  [1:0] HABILITADOR,
  input  H1,
  input  H0,
  input  CANAL_0_bit0,
  input  CANAL_1_bit0,
  input  CANAL_2_bit0,
  input  CANAL_3_bit0,
  input  CANAL_0_bit1,
  input  CANAL_1_bit1,
  input  CANAL_2_bit1,
  input  CANAL_3_bit1,
  input  CANAL_0_bit2,
  input  CANAL_1_bit2,
  input  CANAL_2_bit2,
  input  CANAL_3_bit2,
  output [2:0] SALIDA,
  output bit2,
  output bit1,
  output bit0
);

  wire and_1_out, and_2_out, and_3_out, and_4_out, and_5_out, and_6_out, and_7_out, and_8_out, and_9_out,
       and_10_out, and_11_out, and_12_out, and_13_out, and_14_out, and_15_out, and_16_out, not_1_out,
       not_2_out;

  not not_1 (not_1_out, H1);
  not not_2 (not_2_out, H0);
  Multiplexer #(.select(2), .width(3), .enable("false")) multiplexer_1 (
    .in0(CANAL_0), .in1(CANAL_1), .in2(CANAL_2), .in3(CANAL_3), .out(SALIDA), .sel(HABILITADOR));
  and and_1 (and_1_out, not_1_out, not_2_out);
  and and_2 (and_2_out, not_1_out, H0);
  and and_3 (and_3_out, H1, not_2_out);
  and and_4 (and_4_out, H1, H0);
  and and_5 (and_5_out, and_1_out, CANAL_0_bit0);
  and and_6 (and_6_out, and_2_out, CANAL_1_bit0);
  and and_7 (and_7_out, and_3_out, CANAL_2_bit0);
  and and_8 (and_8_out, and_4_out, CANAL_3_bit0);
  and and_9 (and_9_out, and_1_out, CANAL_0_bit1);
  and and_10 (and_10_out, and_2_out, CANAL_1_bit1);
  and and_11 (and_11_out, and_3_out, CANAL_2_bit1);
  and and_12 (and_12_out, and_4_out, CANAL_3_bit1);
  and and_13 (and_13_out, and_1_out, CANAL_0_bit2);
  and and_14 (and_14_out, and_2_out, CANAL_1_bit2);
  and and_15 (and_15_out, and_3_out, CANAL_2_bit2);
  and and_16 (and_16_out, and_4_out, CANAL_3_bit2);
  or or_1 (bit0, and_5_out, and_6_out, and_7_out, and_8_out);
  or or_2 (bit1, and_9_out, and_10_out, and_11_out, and_12_out);
  or or_3 (bit2, and_13_out, and_14_out, and_15_out, and_16_out);

  // Notes on the sheet:
  //   H1 H0
  //   MUX 4 VIAS / 3 BIT DE LIBRERIA Y CON COMPUERTAS
endmodule
