// Logisim project mux4v4b.circ as structural Verilog: 1 circuit, main circuit main
module main (
  input  [3:0] CANAL_0,
  input  [3:0] CANAL_1,
  input  [3:0] CANAL_2,
  input  [3:0] CANAL_3,
  input  [1:0] HABILITADOR,
  output [3:0] SALIDA
);

  Multiplexer #(.select(2), .width(4), .enable("false")) multiplexer_1 (
    .in0(CANAL_0), .in1(CANAL_1), .in2(CANAL_2), .in3(CANAL_3), .out(SALIDA), .sel(HABILITADOR));
endmodule
