// Logisim project mux8v1bCOMP.circ as structural Verilog: 1 circuit, main circuit main
module main (
  input  CANAL_0,
  input  CANAL_1,
  input  CANAL_2,
  input  CANAL_3,
  input  CANAL_4,
  input  CANAL_5,
  input  CANAL_6,
  input  [2:0] HABILITADOR,
  input  CANAL_7,
  input  H2,
  input  H1,
  input  H0,
  input  CANAL_0_2,
  input  CANAL_1_2,
  input  CANAL_2_2,
  input  CANAL_3_2,
  input  CANAL_4_2,
  input  CANAL_5_2,
  input  CANAL_6_2,
  input  CANAL_7_2,
  output SALIDA,
  output out_22
);

  wire and_1_out, and_2_out, and_3_out, and_4_out, and_5_out, and_6_out, and_7_out, and_8_out, and_9_out,
       and_10_out, and_11_out, and_12_out, and_13_out, and_14_out, and_15_out, and_16_out, not_1_out,
       not_2_out, not_3_out;

  not not_1 (not_1_out, H2);
  not not_2 (not_2_out, H1);
  not not_3 (not_3_out, H0);
  Multiplexer #(.select(3), .enable("false")) multiplexer_1 (
    .in0(CANAL_0), .in1(CANAL_1), .in2(CANAL_2), .in3(CANAL_3), .in4(CANAL_4), .in5(CANAL_5), .in6(CANAL_6),
    .in7(CANAL_7), .out(SALIDA), .sel(HABILITADOR));
  and and_1 (and_1_out, not_1_out, not_2_out, not_3_out);
  and and_2 (and_2_out, not_1_out, not_2_out, H0);
  and and_3 (and_3_out, not_1_out, H1, not_3_out);
  and and_4 (and_4_out, not_1_out, H1, H0);
  and and_5 (and_5_out, H2, not_2_out, not_3_out);
  and and_6 (and_6_out, H2, not_2_out, H0);
  and and_7 (and_7_out, H2, H1, not_3_out);
  and and_8 (and_8_out, H2, H1, H0);
  and and_9 (and_9_out, and_1_out, CANAL_0_2);
  and and_10 (and_10_out, and_2_out, CANAL_1_2);
  and and_11 (and_11_out, and_3_out, CANAL_2_2);
  and and_12 (and_12_out, and_4_out, CANAL_3_2);
  and and_13 (and_13_out, and_5_out, CANAL_4_2);
  and and_14 (and_14_out, and_6_out, CANAL_5_2);
  and and_15 (and_15_out, and_7_out, CANAL_6_2);
  and and_16 (and_16_out, and_8_out, CANAL_7_2);
  or or_1 (out_22, and_9_out, and_10_out, and_11_out, and_12_out, and_13_out, and_14_out, and_15_out, and_16_out);

  // Notes on the sheet:
  //   H2 H1 H0
  //   MUX 8 VIAS / 1 BIT DE LIBRERIA Y CON COMPUERTAS
endmodule
