// Logisim project mux_demux_4v1b.circ as structural Verilog: 1 circuit, main circuit main
module main (
  input  CANAL_0,
  input  CANAL_1,
  input  CANAL_2,
  input  CANAL_3,
  input  [1:0] HABILITADOR,
  output SALIDA_0,
  output SALIDA_1,
  output SALIDA_2,
  output SALIDA_3
);

  wire multiplexer_1_out;

  Multiplexer #(.select(2), .enable("false")) multiplexer_1 (
    .in0(CANAL_0), .in1(CANAL_1), .in2(CANAL_2), .in3(CANAL_3), .out(multiplexer_1_out), .sel(HABILITADOR));
  Demultiplexer #(.select(2), .enable("false")) demultiplexer_1 (
    .out0(SALIDA_0), .out1(SALIDA_1), .out2(SALIDA_2), .out3(SALIDA_3), .in(multiplexer_1_out),
    .sel(HABILITADOR));
endmodule
