// Logisim project mux_demux_4v3b.circ as structural Verilog: 1 circuit, main circuit main
module main (
  input  [2:0] CANAL_0,
  input  [2:0] CANAL_1,
  input  [2:0] CANAL_2,
  input  [2:0] CANAL_3,
  input  [1:0] HABILITADOR,
  output [2:0] SALIDA_0,
  output [2:0] SALIDA_1,
  output [2:0] SALIDA_2,
  output [2:0] SALIDA_3
);

  wire [2:0] multiplexer_1_out;

  Multiplexer #(.select(2), .width(3), .enable("false")) multiplexer_1 (
    .in0(CANAL_0), .in1(CANAL_1), .in2(CANAL_2), .in3(CANAL_3), .out(multiplexer_1_out), .sel(HABILITADOR));
  Demultiplexer #(.select(2), .width(3), .enable("false")) demultiplexer_1 (
    .out0(SALIDA_0), .out1(SALIDA_1), .out2(SALIDA_2), .out3(SALIDA_3), .in(multiplexer_1_out),
    .sel(HABILITADOR));
endmodule
